// Logisim project ESF.circ as structural Verilog: 16 circuits, main circuit main
module main (
);

  wire and_1_out, and_2_out, clock_1_out, multiplexer_1_out;
  wire [4:0] adder_1_out, counter_1_q, subtractor_1_out;
  wire [15:0] keyschedule_1_out_5, multiplexer_2_out, register_1_q;
  wire [31:0] forwardflow_1_out_4, forwardflow_1_out_5, getkey_1_out_3, keyschedule_1_out_6,
       keyschedule_1_out_7, multiplexer_3_out, multiplexer_4_out, multiplexer_5_out, multiplexer_6_out,
       register_2_q, register_3_q, register_4_q, register_5_q;

  Clock clock_1 (.out(clock_1_out));
  Multiplexer multiplexer_1 (.in0(clock_1_out), .in1(1'b1), .out(multiplexer_1_out), .sel(and_1_out));  // open: en
  Counter #(.width(5), .max('h1f)) counter_1 (
    .Q(counter_1_q), .clk(multiplexer_1_out));  // open: load, D, count, carry, clr
  Adder #(.width(5)) adder_1 (.a(counter_1_q), .b(5'b00001), .out(adder_1_out));  // open: cin, cout
  and and_1 (and_1_out, counter_1_q[0], counter_1_q[1], counter_1_q[2], counter_1_q[3], counter_1_q[4]);
  Multiplexer #(.width(16)) multiplexer_2 (
    .in0(register_1_q), .in1(16'h123), .out(multiplexer_2_out), .sel(and_2_out));  // open: en
  Multiplexer #(.width(32)) multiplexer_3 (
    .in0(register_2_q), .in1(32'h456789ab), .out(multiplexer_3_out), .sel(and_2_out));  // open: en
  Multiplexer #(.width(32)) multiplexer_4 (
    .in0(register_3_q), .in1(32'hcdef0123), .out(multiplexer_4_out), .sel(and_2_out));  // open: en
  Multiplexer #(.width(32)) multiplexer_5 (
    .in0(register_4_q), .in1(32'h89abcdef), .out(multiplexer_5_out), .sel(and_2_out));  // open: en
  Multiplexer #(.width(32)) multiplexer_6 (
    .in0(register_5_q), .in1(32'h1234567), .out(multiplexer_6_out), .sel(and_2_out));  // open: en
  Subtractor #(.width(5)) subtractor_1 (.a({5{1'b1}}), .b(counter_1_q), .out(subtractor_1_out));  // open: bin, bout
  and and_2 (and_2_out, subtractor_1_out[4], subtractor_1_out[3], subtractor_1_out[2], subtractor_1_out[1], subtractor_1_out[0]);
  getKey getkey_1 (.in_1(multiplexer_2_out), .in_2(multiplexer_3_out), .out_3(getkey_1_out_3));
  forwardFlow forwardflow_1 (
    .in_1(getkey_1_out_3), .in_2(multiplexer_5_out), .in_3(multiplexer_6_out), .out_4(forwardflow_1_out_4),
    .out_5(forwardflow_1_out_5));
  // Probe on forwardflow_1_out_4
  KeySchedule keyschedule_1 (
    .in_1(multiplexer_2_out), .in_2(multiplexer_3_out), .in_3(multiplexer_4_out), .in_4(adder_1_out),
    .out_5(keyschedule_1_out_5), .out_6(keyschedule_1_out_6), .out_7(keyschedule_1_out_7));
  // Probe on forwardflow_1_out_5
  Register #(.width(16)) register_1 (
    .D(keyschedule_1_out_5), .Q(register_1_q), .clk(multiplexer_1_out));  // open: en, clr
  Register #(.width(32)) register_2 (
    .D(keyschedule_1_out_6), .Q(register_2_q), .clk(multiplexer_1_out));  // open: en, clr
  Register #(.width(32)) register_3 (
    .D(keyschedule_1_out_7), .Q(register_3_q), .clk(multiplexer_1_out));  // open: en, clr
  Register #(.width(32)) register_4 (
    .D(forwardflow_1_out_4), .Q(register_4_q), .clk(multiplexer_1_out));  // open: en, clr
  Register #(.width(32)) register_5 (
    .D(forwardflow_1_out_5), .Q(register_5_q), .clk(multiplexer_1_out));  // open: en, clr
endmodule

module S0 (
  input  [3:0] in_1,
  output [3:0] out_2
);

  Multiplexer #(.select(4), .width(4)) multiplexer_1 (
    .in0(4'b0011), .in1(4'b1000), .in2(4'b1111), .in3(4'b0001), .in4(4'b1010), .in5(4'b0110), .in6(4'b0101),
    .in7(4'b1011), .in8(4'b1110), .in9(4'b1101), .in10(4'b0100), .in11(4'b0010), .in12(4'b0111),
    .in13(4'b0000), .in14(4'b1001), .in15(4'b1100), .out(out_2), .sel(in_1), .en(1'b1));
endmodule

module S1 (
  input  [3:0] in_1,
  output [3:0] out_2
);

  Multiplexer #(.select(4), .width(4)) multiplexer_1 (
    .in0(4'b1111), .in1(4'b1100), .in2(4'b0010), .in3(4'b0111), .in4(4'b1001), .in5(4'b0000), .in6(4'b0101),
    .in7(4'b1010), .in8(4'b0001), .in9(4'b1011), .in10(4'b1110), .in11(4'b1000), .in12(4'b0110),
    .in13(4'b1101), .in14(4'b0011), .in15(4'b0100), .out(out_2), .sel(in_1), .en(1'b1));
endmodule

module S2 (
  input  [3:0] in_1,
  output [3:0] out_2
);

  Multiplexer #(.select(4), .width(4)) multiplexer_1 (
    .in0(4'b1000), .in1(4'b0110), .in2(4'b0111), .in3(4'b1001), .in4(4'b0011), .in5(4'b1100), .in6(4'b1010),
    .in7(4'b1111), .in8(4'b1101), .in9(4'b0001), .in10(4'b1110), .in11(4'b0100), .in12(4'b0000),
    .in13(4'b1011), .in14(4'b0101), .in15(4'b0010), .out(out_2), .sel(in_1), .en(1'b1));
endmodule

module S3 (
  input  [3:0] in_1,
  output [3:0] out_2
);

  Multiplexer #(.select(4), .width(4)) multiplexer_1 (
    .in0(4'b0000), .in1(4'b1111), .in2(4'b1011), .in3(4'b1000), .in4(4'b1100), .in5(4'b1001), .in6(4'b0110),
    .in7(4'b0011), .in8(4'b1101), .in9(4'b0001), .in10(4'b0010), .in11(4'b0100), .in12(4'b1010),
    .in13(4'b0111), .in14(4'b0101), .in15(4'b1110), .out(out_2), .sel(in_1), .en(1'b1));
endmodule

module S4 (
  input  [3:0] in_1,
  output [3:0] out_2
);

  Multiplexer #(.select(4), .width(4)) multiplexer_1 (
    .in0(4'b0001), .in1(4'b1111), .in2(4'b1000), .in3(4'b0011), .in4(4'b1100), .in5(4'b0000), .in6(4'b1011),
    .in7(4'b0110), .in8(4'b0010), .in9(4'b0101), .in10(4'b0100), .in11(4'b1010), .in12(4'b1001),
    .in13(4'b1110), .in14(4'b0111), .in15(4'b1101), .out(out_2), .sel(in_1), .en(1'b1));
endmodule

module S5 (
  input  [3:0] in_1,
  output [3:0] out_2
);

  Multiplexer #(.select(4), .width(4)) multiplexer_1 (
    .in0(4'b1111), .in1(4'b0101), .in2(4'b0010), .in3(4'b1011), .in4(4'b0100), .in5(4'b1010), .in6(4'b1001),
    .in7(4'b1100), .in8(4'b0000), .in9(4'b0011), .in10(4'b1110), .in11(4'b1000), .in12(4'b1101),
    .in13(4'b0110), .in14(4'b0111), .in15(4'b0001), .out(out_2), .sel(in_1), .en(1'b1));
endmodule

module S6 (
  input  [3:0] in_1,
  output [3:0] out_2
);

  Multiplexer #(.select(4), .width(4)) multiplexer_1 (
    .in0(4'b0111), .in1(4'b0010), .in2(4'b1100), .in3(4'b0101), .in4(4'b1000), .in5(4'b0100), .in6(4'b0110),
    .in7(4'b1011), .in8(4'b1110), .in9(4'b1001), .in10(4'b0001), .in11(4'b1111), .in12(4'b1101),
    .in13(4'b0011), .in14(4'b1010), .in15(4'b0000), .out(out_2), .sel(in_1), .en(1'b1));
endmodule

module S7 (
  input  [3:0] in_1,
  output [3:0] out_2
);

  Multiplexer #(.select(4), .width(4)) multiplexer_1 (
    .in0(4'b0001), .in1(4'b1101), .in2(4'b1111), .in3(4'b0000), .in4(4'b1110), .in5(4'b1000), .in6(4'b0010),
    .in7(4'b1011), .in8(4'b0111), .in9(4'b0100), .in10(4'b1100), .in11(4'b1010), .in12(4'b1001),
    .in13(4'b0011), .in14(4'b0101), .in15(4'b0110), .out(out_2), .sel(in_1), .en(1'b1));
endmodule

module pLayer (
  input  [31:0] in_1,
  output [31:0] out_2
);


  assign out_2 = {in_1[31], in_1[27], in_1[23], in_1[19], in_1[15], in_1[11], in_1[7], in_1[3], in_1[30], in_1[26], in_1[22], in_1[18], in_1[14], in_1[10], in_1[6], in_1[2], in_1[29], in_1[25], in_1[21], in_1[17], in_1[13], in_1[9], in_1[5], in_1[1], in_1[28], in_1[24], in_1[20], in_1[16], in_1[12], in_1[8], in_1[4], in_1[0]};
endmodule

module F (
  input  [31:0] in_1,
  input  [31:0] in_2,
  output [31:0] out_3
);

  wire [3:0] s0_1_out_2, s1_1_out_2, s2_1_out_2, s3_1_out_2, s4_1_out_2, s5_1_out_2, s6_1_out_2, s7_1_out_2;
  wire [31:0] xor_1_out;

  assign xor_1_out = in_1 ^ in_2;  // XOR_Gate xor_1, 32 bits wide
  S0 s0_1 (.in_1(xor_1_out[3:0]), .out_2(s0_1_out_2));
  S1 s1_1 (.in_1(xor_1_out[7:4]), .out_2(s1_1_out_2));
  S2 s2_1 (.in_1(xor_1_out[11:8]), .out_2(s2_1_out_2));
  S3 s3_1 (.in_1(xor_1_out[15:12]), .out_2(s3_1_out_2));
  S4 s4_1 (.in_1(xor_1_out[19:16]), .out_2(s4_1_out_2));
  S5 s5_1 (.in_1(xor_1_out[23:20]), .out_2(s5_1_out_2));
  S6 s6_1 (.in_1(xor_1_out[27:24]), .out_2(s6_1_out_2));
  S7 s7_1 (.in_1(xor_1_out[31:28]), .out_2(s7_1_out_2));
  pLayer player_1 (
    .in_1({s7_1_out_2, s6_1_out_2, s5_1_out_2, s4_1_out_2, s3_1_out_2, s2_1_out_2, s1_1_out_2, s0_1_out_2}),
    .out_2(out_3));
endmodule

module LeftRotate (
  input  [15:0] in_1,
  input  [31:0] in_2,
  input  [31:0] in_3,
  output [31:0] out_4,
  output [15:0] out_5,
  output [31:0] out_6
);


  assign out_4 = {in_3[18:0], in_1[15:3]};
  assign out_5 = {in_1[2:0], in_2[31:19]};
  assign out_6 = {in_2[18:0], in_3[31:19]};
endmodule

module KeySchedule (
  input  [15:0] in_1,
  input  [31:0] in_2,
  input  [31:0] in_3,
  input  [4:0] in_4,
  output [15:0] out_5,
  output [31:0] out_6,
  output [31:0] out_7
);

  wire [15:8] leftrotate_1_out_5;
  wire [15:11] leftrotate_1_out_6;

  LeftRotate leftrotate_1 (
    .in_1(in_1), .in_2(in_2), .in_3(in_3), .out_5({leftrotate_1_out_5, out_5[7:0]}),
    .out_6({out_6[31:16], leftrotate_1_out_6, out_6[10:0]}), .out_4(out_7));
  S0 s0_1 (.in_1(leftrotate_1_out_5[11:8]), .out_2(out_5[11:8]));
  S0 s0_2 (.in_1(leftrotate_1_out_5[15:12]), .out_2(out_5[15:12]));
  assign out_6[15:11] = leftrotate_1_out_6 ^ in_4;  // XOR_Gate xor_1, 5 bits wide
endmodule

module getKey (
  input  [15:0] in_1,
  input  [31:0] in_2,
  output [31:0] out_3
);


  assign out_3 = {in_1, in_2[31:16]};
endmodule

module forwardFlow (
  input  [31:0] in_1,
  input  [31:0] in_2,
  input  [31:0] in_3,
  output [31:0] out_4,
  output [31:0] out_5
);

  wire [31:0] f_1_out_3, n7shift_1_out_2;

  F f_1 (.in_1(in_1), .in_2(in_2), .out_3(f_1_out_3));
  _7shift u_7shift_1 (.in_1(in_3), .out_2(n7shift_1_out_2));
  assign out_4 = f_1_out_3 ^ n7shift_1_out_2;  // XOR_Gate xor_1, 32 bits wide

  assign out_5 = in_2;
endmodule

module _7shift (
  input  [31:0] in_1,
  output [31:0] out_2
);


  assign out_2 = {in_1[24:0], in_1[31:25]};
endmodule
