// Logisim project presentCipher.circ as structural Verilog: 8 circuits, main circuit main
module main (
);

  wire and_1_out, clock_1_out;
  wire [4:0] adder_1_out, counter_1_q, subtractor_1_out;
  wire [15:0] keyschedule_1_out_6, multiplexer_3_out, register_1_q;
  wire [31:0] forwardflow_1_out_3, forwardflow_1_out_4, getkey_1_out_5, getkey_1_out_6, getkey_2_out_5,
       getkey_2_out_6, keyschedule_1_out_5, keyschedule_1_out_7, multiplexer_1_out, multiplexer_2_out,
       multiplexer_4_out, multiplexer_5_out, register_2_q, register_3_q, register_4_q, register_5_q,
       roundkey_1_out_3, roundkey_2_out_3, roundkey_3_out_3, roundkey_4_out_3;

  Clock clock_1 (.out(clock_1_out));
  Counter #(.width(5), .max('h1f)) counter_1 (.Q(counter_1_q), .clk(clock_1_out));  // open: load, D, count, carry, clr
  Register #(.width(16)) register_1 (.D(keyschedule_1_out_6), .Q(register_1_q), .clk(clock_1_out));  // open: en, clr
  Register #(.width(32)) register_2 (.D(keyschedule_1_out_5), .Q(register_2_q), .clk(clock_1_out));  // open: en, clr
  Register #(.width(32)) register_3 (.D(keyschedule_1_out_7), .Q(register_3_q), .clk(clock_1_out));  // open: en, clr
  Register #(.width(32)) register_4 (.D(roundkey_3_out_3), .Q(register_4_q), .clk(clock_1_out));  // open: en, clr
  Register #(.width(32)) register_5 (.D(roundkey_4_out_3), .Q(register_5_q), .clk(clock_1_out));  // open: en, clr
  Subtractor #(.width(5)) subtractor_1 (.a({5{1'b1}}), .b(counter_1_q), .out(subtractor_1_out));  // open: bin, bout
  getKey getkey_1 (
    .in_1({32{1'b1}}), .in_2({32{1'b1}}), .in_3({16{1'b1}}), .out_5(getkey_1_out_5), .out_6(getkey_1_out_6));  // open: out_4
  Multiplexer #(.width(32)) multiplexer_1 (
    .in0(register_3_q), .in1({32{1'b1}}), .out(multiplexer_1_out), .sel(and_1_out));  // open: en
  Multiplexer #(.width(32)) multiplexer_2 (
    .in0(register_2_q), .in1({32{1'b1}}), .out(multiplexer_2_out), .sel(and_1_out));  // open: en
  Multiplexer #(.width(16)) multiplexer_3 (
    .in0(register_1_q), .in1({16{1'b1}}), .out(multiplexer_3_out), .sel(and_1_out));  // open: en
  Multiplexer #(.width(32)) multiplexer_4 (
    .in0(register_4_q), .in1(roundkey_1_out_3), .out(multiplexer_4_out), .sel(and_1_out));  // open: en
  Multiplexer #(.width(32)) multiplexer_5 (
    .in0(register_5_q), .in1(roundkey_2_out_3), .out(multiplexer_5_out), .sel(and_1_out));  // open: en
  and and_1 (and_1_out, subtractor_1_out[0], subtractor_1_out[1], subtractor_1_out[2], subtractor_1_out[3], subtractor_1_out[4]);
  RoundKey roundkey_1 (.in_1(getkey_1_out_5), .in_2({32{1'b1}}), .out_3(roundkey_1_out_3));
  RoundKey roundkey_2 (.in_1(getkey_1_out_6), .in_2({32{1'b1}}), .out_3(roundkey_2_out_3));
  KeySchedule keyschedule_1 (
    .in_1(multiplexer_3_out), .in_2(multiplexer_2_out), .in_4(multiplexer_1_out), .in_3(adder_1_out),
    .out_6(keyschedule_1_out_6), .out_5(keyschedule_1_out_5), .out_7(keyschedule_1_out_7));
  Adder #(.width(5)) adder_1 (.a(counter_1_q), .b(5'b00001), .out(adder_1_out));  // open: cin, cout
  // Probe on adder_1_out
  ForwardFlow forwardflow_1 (
    .in_1(multiplexer_4_out), .in_2(multiplexer_5_out), .out_3(forwardflow_1_out_3),
    .out_4(forwardflow_1_out_4));
  // Probe on roundkey_4_out_3
  getKey getkey_2 (
    .in_1(keyschedule_1_out_7), .in_2(keyschedule_1_out_5), .in_3(keyschedule_1_out_6),
    .out_5(getkey_2_out_5), .out_6(getkey_2_out_6));  // open: out_4
  // Probe on roundkey_3_out_3
  RoundKey roundkey_3 (.in_1(getkey_2_out_5), .in_2(forwardflow_1_out_3), .out_3(roundkey_3_out_3));
  RoundKey roundkey_4 (.in_1(getkey_2_out_6), .in_2(forwardflow_1_out_4), .out_3(roundkey_4_out_3));
endmodule

module SLayer (
  input  [3:0] in_1,
  output [3:0] out_2
);

  Multiplexer #(.select(4), .width(4)) multiplexer_1 (
    .in0(4'b1100), .in1(4'b0101), .in2(4'b0110), .in3(4'b1011), .in4(4'b1001), .in5(4'b0000), .in6(4'b1010),
    .in7(4'b1101), .in8(4'b0011), .in9(4'b1110), .in10(4'b1111), .in11(4'b1000), .in12(4'b0100),
    .in13(4'b0111), .in14(4'b0001), .in15(4'b0010), .out(out_2), .sel(in_1), .en(1'b1));
endmodule

module Player (
  input  [31:0] in_1,
  input  [31:0] in_2,
  output [31:0] out_3,
  output [31:0] out_4
);


  assign out_3 = {in_2[29], in_2[25], in_2[21], in_2[17], in_2[13], in_2[9], in_2[5], in_2[1], in_1[29], in_1[25], in_1[21], in_1[17], in_1[13], in_1[9], in_1[5], in_1[1], in_2[28], in_2[24], in_2[20], in_2[16], in_2[12], in_2[8], in_2[4], in_2[0], in_1[28], in_1[24], in_1[20], in_1[16], in_1[12], in_1[8], in_1[4], in_1[0]};
  assign out_4 = {in_2[31], in_2[27], in_2[23], in_2[19], in_2[15], in_2[11], in_2[7], in_2[3], in_1[31], in_1[27], in_1[23], in_1[19], in_1[15], in_1[11], in_1[7], in_1[3], in_2[30], in_2[26], in_2[22], in_2[18], in_2[14], in_2[10], in_2[6], in_2[2], in_1[30], in_1[26], in_1[22], in_1[18], in_1[14], in_1[10], in_1[6], in_1[2]};
endmodule

module KeySchedule (
  input  [15:0] in_1,
  input  [31:0] in_2,
  input  [4:0] in_3,
  input  [31:0] in_4,
  output [31:0] out_5,
  output [15:0] out_6,
  output [31:0] out_7
);

  SLayer slayer_1 (.in_1(in_4[18:15]), .out_2(out_6[15:12]));
  assign out_7[19:15] = in_3 ^ in_2[6:2];  // XOR_Gate xor_1, 5 bits wide

  assign out_5 = {in_4[2:0], in_1, in_2[31:19]};
  assign out_6[11:0] = in_4[14:3];
  assign {out_7[31:20], out_7[14:0]} = {in_2[18:7], in_2[1:0], in_4[31:19]};
endmodule

module getKey (
  input  [31:0] in_1,
  input  [31:0] in_2,
  input  [15:0] in_3,
  output [15:0] out_4,
  output [31:0] out_5,
  output [31:0] out_6
);


  assign out_4 = in_1[15:0];
  assign out_5 = {in_2[15:0], in_1[31:16]};
  assign out_6 = {in_3, in_2[31:16]};
endmodule

module ForwardFlow (
  input  [31:0] in_1,
  input  [31:0] in_2,
  output [31:0] out_3,
  output [31:0] out_4
);

  wire [3:0] slayer_1_out_2, slayer_2_out_2, slayer_3_out_2, slayer_4_out_2, slayer_5_out_2, slayer_6_out_2,
       slayer_7_out_2, slayer_8_out_2, slayer_9_out_2, slayer_10_out_2, slayer_11_out_2, slayer_12_out_2,
       slayer_13_out_2, slayer_14_out_2, slayer_15_out_2, slayer_16_out_2;

  SLayer slayer_1 (.in_1(in_1[3:0]), .out_2(slayer_1_out_2));
  SLayer slayer_2 (.in_1(in_1[7:4]), .out_2(slayer_2_out_2));
  SLayer slayer_3 (.in_1(in_1[11:8]), .out_2(slayer_3_out_2));
  SLayer slayer_4 (.in_1(in_1[15:12]), .out_2(slayer_4_out_2));
  SLayer slayer_5 (.in_1(in_1[19:16]), .out_2(slayer_5_out_2));
  SLayer slayer_6 (.in_1(in_1[23:20]), .out_2(slayer_6_out_2));
  SLayer slayer_7 (.in_1(in_1[27:24]), .out_2(slayer_7_out_2));
  SLayer slayer_8 (.in_1(in_1[31:28]), .out_2(slayer_8_out_2));
  SLayer slayer_9 (.in_1(in_2[3:0]), .out_2(slayer_9_out_2));
  SLayer slayer_10 (.in_1(in_2[7:4]), .out_2(slayer_10_out_2));
  SLayer slayer_11 (.in_1(in_2[11:8]), .out_2(slayer_11_out_2));
  SLayer slayer_12 (.in_1(in_2[15:12]), .out_2(slayer_12_out_2));
  SLayer slayer_13 (.in_1(in_2[19:16]), .out_2(slayer_13_out_2));
  SLayer slayer_14 (.in_1(in_2[23:20]), .out_2(slayer_14_out_2));
  SLayer slayer_15 (.in_1(in_2[27:24]), .out_2(slayer_15_out_2));
  SLayer slayer_16 (.in_1(in_2[31:28]), .out_2(slayer_16_out_2));
  Player player_1 (
    .in_1({slayer_8_out_2, slayer_7_out_2, slayer_6_out_2, slayer_5_out_2, slayer_4_out_2, slayer_3_out_2, slayer_2_out_2, slayer_1_out_2}),
    .in_2({slayer_16_out_2, slayer_15_out_2, slayer_14_out_2, slayer_13_out_2, slayer_12_out_2, slayer_11_out_2, slayer_10_out_2, slayer_9_out_2}),
    .out_3(out_3), .out_4(out_4));
endmodule

module RoundKey (
  input  [31:0] in_1,
  input  [31:0] in_2,
  output [31:0] out_3
);

  assign out_3 = in_1 ^ in_2;  // XOR_Gate xor_1, 32 bits wide
endmodule

module check (
  input  [3:0] in_1,
  input  [3:0] in_2,
  output [3:0] out_3,
  output [3:0] out_4
);

  SLayer slayer_1 (.in_1(in_1), .out_2(out_3));

  assign out_4 = {in_2[0], in_2[2:1], in_2[3]};
endmodule
